// Logisim project 2024-1_R01.circ as structural Verilog: 2 circuits, main circuit main
module main (
  input  a,
  input  b,
  input  c,
  input  d,
  input  a_2,
  input  b_2,
  input  c_2,
  input  d_2,
  input  a_3,
  input  b_3,
  input  c_3,
  input  d_3,
  input  a_4,
  input  b_4,
  input  c_4,
  input  d_4,
  input  a_5,
  input  b_5,
  input  c_5,
  input  d_5,
  input  a_6,
  input  b_6,
  input  c_6,
  input  d_6,
  output s,
  output s_2,
  output s_3,
  output s_4,
  output s_5,
  output s_6
);

  wire and_1_out, and_2_out, and_3_out, and_4_out, and_5_out, and_6_out, and_7_out, and_8_out, and_9_out,
       and_10_out, nand_1_out, nand_2_out, nand_3_out, nor_1_out, nor_2_out, nor_3_out, nor_4_out, not_1_out,
       not_2_out, not_3_out, not_4_out, not_5_out, not_6_out, not_7_out, not_8_out, not_9_out, not_10_out,
       not_11_out, not_12_out, not_13_out, not_14_out, not_15_out, not_16_out, not_17_out, not_18_out,
       not_19_out, not_20_out, not_21_out, not_22_out, not_23_out, not_24_out, not_25_out, not_26_out,
       not_27_out, not_28_out, not_29_out, not_30_out, not_31_out, not_32_out, not_33_out, not_34_out,
       not_35_out, not_36_out, not_37_out, not_38_out, not_39_out, not_40_out, not_41_out, not_42_out,
       not_43_out, not_44_out, not_45_out, not_46_out, not_47_out, not_48_out, not_49_out, not_50_out,
       not_51_out, not_52_out, not_53_out, not_54_out, not_55_out, not_56_out, not_57_out, not_58_out,
       not_59_out, not_60_out, not_61_out, not_62_out, not_63_out, or_1_out, or_2_out, or_3_out, or_4_out,
       or_5_out, or_6_out, or_7_out, or_8_out, or_9_out, or_10_out, or_11_out, or_12_out;

  not not_1 (not_1_out, a);
  not not_2 (not_2_out, b);
  not not_3 (not_3_out, c);
  not not_4 (not_4_out, d);
  not not_5 (not_5_out, a);
  not not_6 (not_6_out, b);
  not not_7 (not_7_out, c);
  not not_8 (not_8_out, a);
  not not_9 (not_9_out, b);
  not not_10 (not_10_out, d);
  not not_11 (not_11_out, a);
  not not_12 (not_12_out, b);
  not not_13 (not_13_out, a);
  not not_14 (not_14_out, c);
  not not_15 (not_15_out, b);
  not not_16 (not_16_out, c);
  not not_17 (not_17_out, d);
  not not_18 (not_18_out, c);
  not not_19 (not_19_out, b_2);
  not not_20 (not_20_out, b_2);
  not not_21 (not_21_out, c_2);
  not not_22 (not_22_out, b_2);
  not not_23 (not_23_out, c_2);
  not not_24 (not_24_out, d_2);
  not not_25 (not_25_out, a_2);
  not not_26 (not_26_out, d_2);
  not not_27 (not_27_out, a_2);
  not not_28 (not_28_out, c_2);
  not not_29 (not_29_out, a_2);
  not not_30 (not_30_out, c_2);
  not not_31 (not_31_out, d_2);
  not not_32 (not_32_out, a_2);
  not not_33 (not_33_out, b_2);
  not not_34 (not_34_out, a_2);
  not not_35 (not_35_out, b_2);
  not not_36 (not_36_out, c_2);
  not not_37 (not_37_out, d_2);
  not not_38 (not_38_out, c_3);
  not not_39 (not_39_out, d_3);
  not not_40 (not_40_out, b_3);
  not not_41 (not_41_out, a_3);
  not not_42 (not_42_out, b_3);
  not not_43 (not_43_out, c_3);
  not not_44 (not_44_out, c_4);
  not not_45 (not_45_out, b_4);
  not not_46 (not_46_out, c_4);
  not not_47 (not_47_out, a_4);
  not not_48 (not_48_out, b_4);
  not not_49 (not_49_out, a_4);
  not not_50 (not_50_out, d_4);
  not not_51 (not_51_out, c_5);
  not not_52 (not_52_out, d_5);
  not not_53 (not_53_out, b_5);
  not not_54 (not_54_out, a_5);
  not not_55 (not_55_out, b_5);
  not not_56 (not_56_out, c_5);
  and and_1 (and_1_out, not_1_out, not_2_out, not_3_out, not_4_out);
  and and_2 (and_2_out, not_5_out, not_6_out, not_7_out, d);
  and and_3 (and_3_out, not_8_out, not_9_out, c, not_10_out);
  and and_4 (and_4_out, not_11_out, not_12_out, c, d);
  and and_5 (and_5_out, not_13_out, b, not_14_out, d);
  and and_6 (and_6_out, a, not_15_out, not_16_out, not_17_out);
  and and_7 (and_7_out, a, b, not_18_out, d);
  or or_1 (or_1_out, a_2, not_19_out, c_2, d_2);
  or or_2 (or_2_out, a_2, not_20_out, not_21_out, d_2);
  or or_3 (or_3_out, a_2, not_22_out, not_23_out, not_24_out);
  or or_4 (or_4_out, not_25_out, b_2, c_2, not_26_out);
  or or_5 (or_5_out, not_27_out, b_2, not_28_out, d_2);
  or or_6 (or_6_out, not_29_out, b_2, not_30_out, not_31_out);
  or or_7 (or_7_out, not_32_out, not_33_out, c_2, d_2);
  or or_8 (or_8_out, not_34_out, not_35_out, not_36_out, not_37_out);
  and and_8 (and_8_out, not_38_out, not_39_out, not_40_out);
  and and_9 (and_9_out, not_41_out, not_42_out);
  and and_10 (and_10_out, not_43_out, d_3, b_3);
  or or_9 (or_9_out, not_44_out, not_45_out);
  or or_10 (or_10_out, not_46_out, not_47_out);
  or or_11 (or_11_out, not_48_out, d_4);
  or or_12 (or_12_out, not_49_out, b_4, not_50_out);
  not not_57 (not_57_out, c_6);
  not not_58 (not_58_out, b_6);
  not not_59 (not_59_out, c_6);
  not not_60 (not_60_out, a_6);
  not not_61 (not_61_out, b_6);
  not not_62 (not_62_out, a_6);
  not not_63 (not_63_out, d_6);
  or or_13 (s, and_1_out, and_2_out, and_3_out, and_4_out, and_5_out, and_6_out, and_7_out);
  or or_14 (s_3, and_8_out, and_9_out, and_10_out);
  and and_11 (s_4, or_9_out, or_10_out, or_11_out, or_12_out);
  nand nand_1 (nand_1_out, not_51_out, not_52_out, not_53_out);
  nand nand_2 (nand_2_out, not_54_out, not_55_out);
  nand nand_3 (nand_3_out, not_56_out, d_5, b_5);
  nor nor_1 (nor_1_out, not_57_out, not_58_out);
  nor nor_2 (nor_2_out, not_59_out, not_60_out);
  nor nor_3 (nor_3_out, not_61_out, d_6);
  nor nor_4 (nor_4_out, not_62_out, b_6, not_63_out);
  and and_12 (s_2, or_1_out, or_2_out, or_3_out, or_4_out, or_5_out, or_6_out, or_7_out, or_8_out);
  or or_15 (s_5, nand_1_out, nand_2_out, nand_3_out);
  nand nand_4 (s_6, nor_1_out, nor_2_out, nor_3_out, nor_4_out);

  // Notes on the sheet:
  //   2024-1_R01
  //   1a) 
  //   b)
  //   ;
  //   C)
  //   d)
  //   e)
  //   f)
endmodule

module _1f (
  input  a,
  input  b,
  input  c,
  input  d,
  output s
);

  wire nor_1_out, nor_2_out, nor_3_out, nor_4_out, not_1_out, not_2_out, not_3_out, not_4_out, not_5_out,
       not_6_out, not_7_out;

  not not_1 (not_1_out, c);
  not not_2 (not_2_out, b);
  not not_3 (not_3_out, c);
  not not_4 (not_4_out, a);
  not not_5 (not_5_out, b);
  not not_6 (not_6_out, a);
  not not_7 (not_7_out, d);
  nor nor_1 (nor_1_out, not_1_out, not_2_out);
  nor nor_2 (nor_2_out, not_3_out, not_4_out);
  nor nor_3 (nor_3_out, not_5_out, d);
  nor nor_4 (nor_4_out, not_6_out, b, not_7_out);
  nand nand_1 (s, nor_1_out, nor_2_out, nor_3_out, nor_4_out);
endmodule
