// Logisim project 2024-1_R02.circ as structural Verilog: 1 circuit, main circuit main
module main (
  input  A,
  input  B_prime,
  input  A_2,
  input  B,
  input  A_prime,
  input  B_2,
  input  C,
  input  A_3,
  input  B_3,
  input  C_2,
  input  A_prime_2,
  input  B_4,
  input  A_prime_3,
  input  C_3,
  input  A_4,
  input  B_5,
  input  C_4,
  input  A_prime_4,
  input  B_6,
  input  C_5,
  input  in_21,
  input  in_22,
  input  in_23,
  input  in_24,
  output S,
  output S_2,
  output S_3,
  output S_4,
  output S_5,
  output Q3,
  output Q2,
  output Q1,
  output Q0,
  output Q0_2,
  output Q1_2,
  output Q2_2,
  output Q3_2,
  output Q3_3,
  output Q2_3,
  output Q1_3,
  output Q0_3,
  output Q3_4,
  output Q2_4,
  output Q1_4,
  output Q0_4
);

  wire and_1_out, and_2_out, and_4_out, and_5_out, and_6_out, and_7_out, and_8_out, clock_1_out, clock_2_out,
       clock_3_out, clock_4_out, nand_1_out, not_1_out, not_2_out, not_3_out, not_4_out, not_5_out, xor_1_out;

  Clock clock_1 (.out(clock_1_out));
  Clock clock_2 (.out(clock_2_out));
  Clock clock_3 (.out(clock_3_out));
  Clock clock_4 (.out(clock_4_out));
  and and_1 (and_1_out, A, not_1_out);
  not not_1 (not_1_out, B_prime);
  and and_2 (and_2_out, A_2, B);
  not not_2 (not_2_out, A_prime);
  and and_3 (S_3, B_3, C_2);
  not not_3 (not_3_out, A_prime_2);
  not not_4 (not_4_out, A_prime_3);
  and and_4 (and_4_out, A_4, B_5, C_4);
  not not_5 (not_5_out, A_prime_4);
  and and_5 (and_5_out, not_5_out, B_6, C_5);
  D_Flip_Flop d_ff_1 (.clk(clock_1_out), .D(in_21), .Q(Q3));  // open: Qn, preset, en, reset
  D_Flip_Flop d_ff_2 (.clk(clock_2_out), .D(in_22), .Q(Q0_2));  // open: Qn, preset, en, reset
  D_Flip_Flop d_ff_3 (.clk(clock_3_out), .D(xor_1_out), .Q(Q3_3));  // open: Qn, preset, en, reset
  xor xor_1 (xor_1_out, in_23, in_23);
  D_Flip_Flop d_ff_4 (.clk(clock_4_out), .D(nand_1_out), .Q(Q3_4));  // open: Qn, preset, en, reset
  nand nand_1 (nand_1_out, in_24, in_24);
  and and_6 (and_6_out, not_2_out, B_2, C);
  and and_7 (and_7_out, not_3_out, B_4);
  and and_8 (and_8_out, not_4_out, C_3);
  T_Flip_Flop t_ff_1 (.clk(clock_1_out), .T(Q3), .Q(Q2));  // open: Qn, preset, reset, en
  T_Flip_Flop t_ff_2 (.clk(clock_2_out), .T(Q0_2), .Q(Q1_2));  // open: Qn, preset, reset, en
  T_Flip_Flop t_ff_3 (.clk(clock_3_out), .T(Q3_3), .Q(Q2_3));  // open: Qn, preset, reset, en
  T_Flip_Flop t_ff_4 (.clk(clock_4_out), .T(Q3_4), .Q(Q2_4));  // open: Qn, preset, reset, en
  or or_1 (S, and_1_out, and_2_out);
  or or_2 (S_2, and_6_out, A_3);
  or or_3 (S_4, and_7_out, and_8_out);
  or or_4 (S_5, and_4_out, and_5_out);
  D_Flip_Flop d_ff_5 (.clk(clock_1_out), .D(Q2), .Q(Q1));  // open: Qn, preset, en, reset
  D_Flip_Flop d_ff_6 (.clk(clock_2_out), .D(Q1_2), .Q(Q2_2));  // open: Qn, preset, en, reset
  D_Flip_Flop d_ff_7 (.clk(clock_3_out), .D(Q2_3), .Q(Q1_3));  // open: Qn, preset, en, reset
  D_Flip_Flop d_ff_8 (.clk(clock_4_out), .D(Q2_4), .Q(Q1_4));  // open: Qn, preset, en, reset
  D_Flip_Flop d_ff_9 (.clk(clock_1_out), .D(Q1), .Q(Q0));  // open: Qn, preset, en, reset
  D_Flip_Flop d_ff_10 (.clk(clock_2_out), .D(Q2_2), .Q(Q3_2));  // open: Qn, preset, en, reset
  D_Flip_Flop d_ff_11 (.clk(clock_3_out), .D(Q1_3), .Q(Q0_3));  // open: Qn, preset, en, reset
  D_Flip_Flop d_ff_12 (.clk(clock_4_out), .D(Q1_4), .Q(Q0_4));  // open: Qn, preset, en, reset

  // Notes on the sheet:
  //   a) Da
  //   b) JaKa
  //   c) Ta
  //   d) SbRb
  //   e) Tb
  //   5 - Montar shifters
  //   a)
  //   b)
  //   c)
  //   d)
  //   4 - Montar os circuitos correspondentes 
endmodule
