// Logisim project 2024-1_guia04.circ as structural Verilog: 10 circuits, main circuit Q01a
module Q01a (
  input  x,
  input  y,
  input  z,
  output s
);

  wire nand_1_out, not_2_out, NOT_3_out, NOT_out;

  not NOT (NOT_out, y);
  not not_2 (not_2_out, z);
  not NOT_3 (NOT_3_out, x);
  nand nand_1 (nand_1_out, NOT_out, not_2_out);
  or or_1 (s, NOT_3_out, nand_1_out);

  // Notes on the sheet:
  //   NOT
  //   AND
  //   OR
  //   Questao 01: 
  //   a)  x' + (y' . z')' 
endmodule

module Q01b (
  input  x,
  input  y,
  input  z,
  output s
);

  wire nor_1_out, not_1_out;

  not not_1 (not_1_out, y);
  nor nor_1 (nor_1_out, x, not_1_out);
  and and_1 (s, nor_1_out, z);

  // Notes on the sheet:
  //   NOT
  //   OR
  //   AND
  //   b) (x + y')' . z
endmodule

module Q01c (
  input  x,
  input  y,
  input  z,
  output s
);

  wire nand_1_out, not_1_out, not_2_out, not_3_out;

  not not_1 (not_1_out, x);
  not not_2 (not_2_out, y);
  nand nand_1 (nand_1_out, not_1_out, not_2_out);
  not not_3 (not_3_out, z);
  and and_1 (s, nand_1_out, not_3_out);

  // Notes on the sheet:
  //   NOT
  //   NOT
  //   AND
  //   NOT
  //   AND
  //   c) (x' . y)' . z'
endmodule

module Q01d (
  input  x,
  input  y,
  input  z,
  output s
);

  wire nand_1_out, not_1_out, not_2_out;

  not not_1 (not_1_out, x);
  not not_2 (not_2_out, y);
  nand nand_1 (nand_1_out, not_1_out, not_2_out);
  and and_1 (s, nand_1_out, z);

  // Notes on the sheet:
  //   NOT
  //   NOT
  //   obs: então da a entender pelo
  //   circuito que (x' . y') ' . z = x' . y ' . z
  //   (não sei se está certo 
  //   qualquer coisa, perdão theldo kkkk)
  //   AND
  //   AND
  //   d) (x' . y')' . z
endmodule

module Q01e (
  input  x,
  input  y,
  input  z,
  output s
);

  wire nor_1_out, not_1_out, or_1_out;

  not not_1 (not_1_out, y);
  Q01b q01b_1 (.x(z));  // open: y, z, s
  or or_1 (or_1_out, x, y);
  nor nor_1 (nor_1_out, not_1_out, z);
  and and_1 (s, or_1_out, nor_1_out);

  // Notes on the sheet:
  //   NOT
  //   OR
  //   OR
  //   AND
  //   e) (x + y) . ( y' + z)'
endmodule

module Q02a (
  input  x,
  input  y,
  output s
);

  wire nor_1_out, not_1_out, not_2_out;

  not not_1 (not_1_out, x);
  not not_2 (not_2_out, y);
  nor nor_1 (nor_1_out, not_1_out, not_2_out);
  and and_1 (s, x, nor_1_out);

  // Notes on the sheet:
  //   NOT
  //   NOT
  //   OR
  //   AND
  //   Questão 02:
  //   a) x . (x' + y')'
endmodule

module Q02b (
  input  x,
  input  y,
  output s
);

  wire and_1_out, not_1_out;

  not not_1 (not_1_out, x);
  and and_1 (and_1_out, x, y);
  or or_1 (s, not_1_out, y, and_1_out);

  // Notes on the sheet:
  //   b) (x' + y) + (x . y)
endmodule

module Q02c (
  input  x,
  input  y,
  output s
);

  wire nand_1_out, not_1_out, or_1_out;

  not not_1 (not_1_out, y);
  nand nand_1 (nand_1_out, x, y);
  or or_1 (or_1_out, x, not_1_out);
  and and_1 (s, nand_1_out, or_1_out);

  // Notes on the sheet:
  //   c) (x' + y)' . ( x + y')
endmodule

module Q02d (
  input  x,
  input  y,
  output s
);

  wire nand_1_out, nor_1_out, not_1_out, not_2_out, not_3_out, not_4_out;

  not not_1 (not_1_out, x);
  not not_2 (not_2_out, y);
  not not_3 (not_3_out, x);
  not not_4 (not_4_out, y);
  nand nand_1 (nand_1_out, not_1_out, not_2_out);
  nor nor_1 (nor_1_out, not_3_out, not_4_out);
  or or_1 (s, nand_1_out, nor_1_out);

  // Notes on the sheet:
  //   d) (x' . y')' + (x' + y')'
endmodule

module Q02e (
  input  x,
  input  y,
  output s
);

  wire nor_1_out, nor_2_out, not_1_out;

  not not_1 (not_1_out, x);
  Q01e q01e_1 ();  // open: x, y, z, s
  nor nor_1 (nor_1_out, y, not_1_out);
  nor nor_2 (nor_2_out, y, x);
  and and_1 (s, nor_1_out, nor_2_out);

  // Notes on the sheet:
  //   e) (y + x')' . (y' + x)
endmodule
