// Logisim project 2024-1_guia05.circ as structural Verilog: 1 circuit, main circuit main
module main (
  input  A,
  input  B,
  input  A_2,
  input  B_2,
  input  A_3,
  input  B_3,
  input  A_4,
  input  B_4,
  input  A_5,
  input  B_5,
  input  A_6,
  input  B_6,
  input  A_7,
  input  B_7,
  input  A_8,
  input  B_8,
  output s,
  output s_2,
  output s_3,
  output s_4,
  output s_5,
  output s_6,
  output s_7,
  output s_8
);

  wire and_1_out, not_1_out, not_2_out, not_3_out, not_4_out, not_5_out, not_6_out, not_7_out, not_8_out,
       or_1_out, or_2_out, xor_1_out, xor_2_out;

  not not_1 (not_1_out, A_4);
  xor xor_1 (xor_1_out, A_6, B_6);
  not not_2 (not_2_out, A_7);
  not not_3 (not_3_out, B_7);
  not not_4 (not_4_out, A_8);
  not not_5 (not_5_out, B_8);
  not not_6 (not_6_out, B);
  not not_7 (not_7_out, A_2);
  not not_8 (not_8_out, A_3);
  xor xor_2 (xor_2_out, A_5, B_5);
  nand nand_1 (s_6, xor_1_out, xor_1_out);
  nand nand_2 (s_8, not_4_out, not_5_out);
  and and_1 (and_1_out, A, not_6_out);
  or or_1 (or_1_out, not_7_out, B_2);
  or or_2 (or_2_out, not_8_out, B_3);
  nand nand_3 (s_4, not_1_out, B_4);
  nor nor_1 (s_5, xor_2_out, xor_2_out, xor_2_out, xor_2_out, xor_2_out);
  nor nor_2 (s_7, not_2_out, not_3_out);
  nor nor_3 (s, and_1_out, and_1_out, and_1_out, and_1_out, and_1_out);
  nand nand_4 (s_2, or_1_out, or_1_out, or_1_out, or_1_out, or_1_out);
  nor nor_4 (s_3, or_2_out, or_2_out, or_2_out, or_2_out, or_2_out);

  // Notes on the sheet:
  //   01)
  //   02)
  //   03)
  //   05)
  //   NOT
  //   (~a | b )
  //   04)  ~(~a & b) usando a porta nand
  //   06) (a^b =a xor b) usando nand
  //   07) ~(~a ^ ~b) usando porta nor 
  //   08) ~(~a & ~b) usando porta nand
  //   (a & ~b) usando portas nor
  //   NOT
  //   (~a | b ) usando a porta nand
  //   usando a porta nor
  //   (~(a ^ b) = a xor b) usando a porta nor
  //   AND
  //   NOR
  //   NAND
  //   2024-1_guia05 
  //   Nome: Felipe Vilhena Dias
  //   Matricula : 81724
endmodule
