// Logisim project 2024-1_guia06.circ as structural Verilog: 3 circuits, main circuit main
module main (
  input  in_1,
  input  in_2,
  input  in_3,
  input  in_4,
  input  in_5,
  input  in_6,
  input  in_7,
  output out_8,
  output out_9
);

  wire and_1_out, and_2_out, and_3_out, and_4_out, and_5_out, nand_1_out, not_1_out, not_2_out, not_3_out,
       not_4_out, not_5_out, not_6_out, not_7_out, not_8_out, not_9_out, not_10_out, not_11_out, not_12_out,
       not_13_out, or_1_out, or_2_out, or_3_out, or_4_out;

  not not_1 (not_1_out, in_2);
  not not_2 (not_2_out, in_1);
  not not_3 (not_3_out, in_1);
  and and_1 (and_1_out, in_3, in_2);
  not not_4 (not_4_out, in_6);
  and and_2 (and_2_out, in_7, in_6, in_5);
  or or_1 (or_1_out, not_1_out, not_2_out);
  and and_3 (and_3_out, in_2, in_1, in_1);
  or or_2 (or_2_out, and_1_out, not_3_out);
  not not_5 (not_5_out, in_5);
  not not_6 (not_6_out, in_4);
  not not_7 (not_7_out, in_4);
  not not_8 (not_8_out, or_1_out);
  not not_9 (not_9_out, and_3_out);
  not not_10 (not_10_out, or_2_out);
  or or_3 (or_3_out, not_5_out, in_6, not_6_out);
  and and_4 (and_4_out, in_5, not_4_out, in_4);
  or or_4 (or_4_out, and_2_out, not_7_out);
  nand nand_1 (nand_1_out, not_8_out, not_9_out);
  not not_11 (not_11_out, or_3_out);
  not not_12 (not_12_out, and_4_out);
  not not_13 (not_13_out, or_4_out);
  or or_5 (out_8, nand_1_out, not_10_out);
  and and_5 (and_5_out, not_11_out, not_12_out);
  or or_6 (out_9, and_5_out, not_13_out);
endmodule

module _07 (
  input  X,
  input  Y,
  input  Z,
  output s
);

  wire and_1_out, and_2_out, and_3_out, not_1_out, not_2_out, not_3_out, not_4_out;

  not not_1 (not_1_out, Y);
  not not_2 (not_2_out, Z);
  not not_3 (not_3_out, X);
  not not_4 (not_4_out, Y);
  and and_1 (and_1_out, X, not_1_out, not_2_out);
  and and_2 (and_2_out, not_3_out, Y, Z);
  and and_3 (and_3_out, X, not_4_out, Z);
  or or_1 (s, and_1_out, and_2_out, and_3_out);
endmodule

module _08 (
  input  f,
  input  w,
  input  x,
  input  y,
  input  z,
  output s
);

  wire and_1_out, and_2_out, and_3_out, and_4_out, not_1_out, not_2_out, not_3_out, not_4_out, not_5_out,
       not_6_out, not_7_out;

  not not_1 (not_1_out, y);
  not not_2 (not_2_out, z);
  not not_3 (not_3_out, x);
  not not_4 (not_4_out, y);
  not not_5 (not_5_out, w);
  not not_6 (not_6_out, x);
  not not_7 (not_7_out, z);
  and and_1 (and_1_out, w, x, y, z);
  and and_2 (and_2_out, w, x, not_1_out, not_2_out);
  and and_3 (and_3_out, w, not_3_out, not_4_out, z);
  and and_4 (and_4_out, not_5_out, not_6_out, y, not_7_out);
  or or_1 (s, and_1_out, and_2_out, and_3_out, and_4_out);
endmodule
