// Logisim project 2024-1_guia07.circ as structural Verilog: 1 circuit, main circuit main
module main (
  input  _01,
  input  in_2,
  input  in_3,
  input  in_4,
  input  A,
  input  B,
  input  C,
  input  D,
  input  in_9,
  output out_10,
  output out_11,
  output out_12,
  output out_13,
  output out_14,
  output out_15
);

  wire and_2_out, nand_2_out, nor_2_out, or_2_out;

  and and_1 (out_10, _01, in_2);
  nand nand_1 (out_11, _01, in_2);
  or or_1 (out_12, in_4, in_3);
  nor nor_1 (out_13, in_4, in_3);
  and and_2 (and_2_out, A, A);
  nand nand_2 (nand_2_out, A, A);
  or or_2 (or_2_out, A, A);
  nor nor_2 (nor_2_out, A, A);
  // Multiplexer multiplexer_1: pin names not known; wires that end beside it: and_2_out, nand_2_out, out_14
  // Multiplexer multiplexer_2: pin names not known; wires that end beside it: or_2_out, nor_2_out, out_15

  assign B = A;
  assign C = A;
  assign D = A;

  // Notes on the sheet:
  //   02)
  //   03)
  //   04)
endmodule
