// Logisim project 2024-1_guia08.circ as structural Verilog: 4 circuits, main circuit main
module main (
  input  B4,
  input  B3,
  input  B2,
  input  B1,
  input  B0,
  input  A4,
  input  A3,
  input  A2,
  input  A1,
  input  A0,
  input  A4_2,
  input  A3_2,
  input  A2_2,
  input  A1_2,
  input  A0_2,
  input  B4_2,
  input  B3_2,
  input  B2_2,
  input  B1_2,
  input  B0_2,
  input  A0_3,
  input  B0_3,
  input  A1_3,
  input  B0_4,
  input  A2_3,
  input  B2_3,
  input  A0_4,
  input  B0_5,
  input  A1_4,
  input  B0_6,
  input  A2_4,
  input  B2_4,
  input  B4_3,
  input  B3_3,
  input  B2_5,
  input  B1_3,
  input  B0_7,
  output C5,
  output S4,
  output S3,
  output S2,
  output S1,
  output C0,
  output S0,
  output Bi0,
  output D4,
  output D3,
  output D2,
  output D1,
  output D0,
  output Bo5,
  output AneBn,
  output AndBn,
  output C5_2,
  output S4_2,
  output S3_2,
  output S2_2,
  output S1_2,
  output C0_2,
  output S0_2
);

  wire and_2_out, complemento_de_1_1_s0, complemento_de_1_1_s1, complemento_de_1_1_s2, complemento_de_1_1_s3,
       complemento_de_1_1_s4, not_1_out, not_2_out, not_3_out, not_4_out, not_5_out, not_6_out,
       somador_de_1bit_1_cout, somador_de_1bit_2_cout, somador_de_1bit_3_cout, somador_de_1bit_4_cout,
       somador_de_1bit_6_cout, somador_de_1bit_7_cout, somador_de_1bit_8_cout, somador_de_1bit_9_cout,
       subtrador_de_1bit_1_bout, subtrador_de_1bit_3_bout, subtrador_de_1bit_4_bout, xor_1_out, xor_2_out,
       xor_3_out, xor_4_out, xor_5_out, xor_6_out;

  somador_de_1bit somador_de_1bit_1 (.B(B4), .Cin(C5), .A(A4), .Cout(somador_de_1bit_1_cout), .S(S4));
  somador_de_1bit somador_de_1bit_2 (
    .B(B3), .Cin(somador_de_1bit_1_cout), .A(A3), .Cout(somador_de_1bit_2_cout), .S(S3));
  somador_de_1bit somador_de_1bit_3 (
    .B(B2), .Cin(somador_de_1bit_2_cout), .A(A2), .Cout(somador_de_1bit_3_cout), .S(S2));
  somador_de_1bit somador_de_1bit_4 (
    .B(B1), .Cin(somador_de_1bit_3_cout), .A(A1), .Cout(somador_de_1bit_4_cout), .S(S1));
  somador_de_1bit somador_de_1bit_5 (.B(B0), .Cin(somador_de_1bit_4_cout), .A(A0), .Cout(C0), .S(S0));
  subtrador_de_1bit subtrador_de_1bit_1 (.A(A0_2), .B(B0_2), .Bin(Bi0), .D(D4), .Bout(subtrador_de_1bit_1_bout));
  subtrador_de_1bit subtrador_de_1bit_2 (.A(A1_2), .B(B1_2), .Bin(subtrador_de_1bit_1_bout), .D(B0_2));  // open: Bout
  subtrador_de_1bit subtrador_de_1bit_3 (.A(A2_2), .B(B2_2), .D(B0_2), .Bout(subtrador_de_1bit_3_bout));  // open: Bin
  subtrador_de_1bit subtrador_de_1bit_4 (
    .A(A3_2), .B(B3_2), .Bin(subtrador_de_1bit_3_bout), .D(B0_2), .Bout(subtrador_de_1bit_4_bout));
  subtrador_de_1bit subtrador_de_1bit_5 (.A(A4_2), .B(B4_2), .Bin(subtrador_de_1bit_4_bout), .D(B0_2), .Bout(Bo5));
  somador_de_1bit somador_de_1bit_6 (
    .B(complemento_de_1_1_s4), .Cin(C5_2), .A(1'b0), .Cout(somador_de_1bit_6_cout), .S(S4_2));
  somador_de_1bit somador_de_1bit_7 (
    .B(complemento_de_1_1_s3), .Cin(somador_de_1bit_6_cout), .A(1'b0), .Cout(somador_de_1bit_7_cout), .S(S3_2));
  somador_de_1bit somador_de_1bit_8 (
    .B(complemento_de_1_1_s2), .Cin(somador_de_1bit_7_cout), .A(1'b0), .Cout(somador_de_1bit_8_cout), .S(S2_2));
  somador_de_1bit somador_de_1bit_9 (
    .B(complemento_de_1_1_s1), .Cin(somador_de_1bit_8_cout), .A(1'b0), .Cout(somador_de_1bit_9_cout), .S(S1_2));
  somador_de_1bit somador_de_1bit_10 (
    .B(complemento_de_1_1_s0), .Cin(somador_de_1bit_9_cout), .A(1'b1), .Cout(C0_2), .S(S0_2));
  xor xor_1 (xor_1_out, A0_3, B0_3);
  xor xor_2 (xor_2_out, A1_3, B0_4);
  xor xor_3 (xor_3_out, A2_3, B2_3);
  xor xor_4 (xor_4_out, A0_4, B0_5);
  xor xor_5 (xor_5_out, A1_4, B0_6);
  xor xor_6 (xor_6_out, A2_4, B2_4);
  not not_1 (not_1_out, xor_1_out);
  not not_2 (not_2_out, xor_2_out);
  not not_3 (not_3_out, xor_3_out);
  not not_4 (not_4_out, xor_4_out);
  not not_5 (not_5_out, xor_5_out);
  not not_6 (not_6_out, xor_6_out);
  complemento_de_1 complemento_de_1_1 (
    .A4(B4_3), .A3(B3_3), .A2(B2_5), .A1(B1_3), .A0(B0_7), .S4(complemento_de_1_1_s4),
    .S3(complemento_de_1_1_s3), .S2(complemento_de_1_1_s2), .S1(complemento_de_1_1_s1),
    .S0(complemento_de_1_1_s0));
  and and_1 (AneBn, not_1_out, not_2_out, not_3_out);
  and and_2 (and_2_out, not_4_out, not_5_out, not_6_out);
  not not_7 (AndBn, and_2_out);

  assign D0 = B0_2;
  assign D1 = B0_2;
  assign D2 = B0_2;
  assign D3 = B0_2;

  // Notes on the sheet:
  //   2024-1_guia08
  //   2) Subtrador 5bits
  //   3) Igualdade 6bits
  //   1) Somador com 5 bits
  //   4) Desigualdade 6bits
  //   5) Complemento de 2 com 5 bits
endmodule

module somador_de_1bit (
  input  B,
  input  Cin,
  input  A,
  output Cout,
  output S
);

  wire and_1_out, and_2_out, and_3_out, xor_1_out;

  xor xor_1 (xor_1_out, A, B);
  and and_1 (and_1_out, B, A);
  and and_2 (and_2_out, B, Cin);
  and and_3 (and_3_out, A, Cin);
  xor xor_2 (S, xor_1_out, Cin);
  or or_1 (Cout, and_1_out, and_2_out, and_3_out);
endmodule

module subtrador_de_1bit (
  input  A,
  input  B,
  input  Bin,
  output D,
  output Bout
);

  wire and_1_out, and_2_out, not_1_out, not_2_out, xor_1_out;

  not not_1 (not_1_out, A);
  xor xor_1 (xor_1_out, A, B);
  and and_1 (and_1_out, B, not_1_out);
  not not_2 (not_2_out, xor_1_out);
  xor xor_2 (D, xor_1_out, Bin);
  and and_2 (and_2_out, Bin, not_2_out);
  or or_1 (Bout, and_2_out, and_1_out);

  // Notes on the sheet:
  //   È uma soma completa, mas nao consegui mudar o nome do arquivo
endmodule

module complemento_de_1 (
  input  A4,
  input  A3,
  input  A2,
  input  A1,
  input  A0,
  output S4,
  output S3,
  output S2,
  output S1,
  output S0
);

  not not_1 (S3, A3);
  not not_2 (S4, A4);
  not not_3 (S1, A1);
  not not_4 (S2, A2);
  not not_5 (S0, A0);
endmodule
