// Logisim project 2024-1_guia14.circ as structural Verilog: 1 circuit, main circuit main
module main (
  input  in_1
);

  wire and_1_out, and_2_out, and_3_out, clock_1_out, d_ff_1_q, d_ff_2_q, d_ff_3_q, d_ff_4_q, d_ff_5_q;

  Clock clock_1 (.out(clock_1_out));
  D_Flip_Flop d_ff_1 (.clk(in_1), .D(in_1), .Q(d_ff_1_q));  // open: Qn, preset, en, reset
  D_Flip_Flop d_ff_2 (.clk(d_ff_1_q), .D(d_ff_1_q), .Q(d_ff_2_q));  // open: Qn, preset, en, reset
  LED led_1 (.in(d_ff_5_q));
  and and_1 (and_1_out, d_ff_1_q, d_ff_2_q);
  LED led_2 (.in(d_ff_3_q));
  LED led_3 (.in(d_ff_4_q));
  D_Flip_Flop d_ff_3 (.clk(and_1_out), .D(and_1_out), .Q(d_ff_3_q));  // open: Qn, preset, en, reset
  LED led_4 (.in(d_ff_2_q));
  and and_2 (and_2_out, and_1_out, d_ff_3_q);
  LED led_5 (.in(d_ff_1_q));
  D_Flip_Flop d_ff_4 (.clk(and_2_out), .D(and_2_out), .Q(d_ff_4_q));  // open: Qn, preset, en, reset
  and and_3 (and_3_out, and_2_out, d_ff_4_q);
  D_Flip_Flop d_ff_5 (.clk(and_3_out), .D(and_3_out), .Q(d_ff_5_q));  // open: Qn, preset, en, reset

  // Notes on the sheet:
  //   1)
  //   2)
  //   5 bits
  //   4 bits
  //   3 bits
  //   2 bits
  //   1 bits
endmodule
