// Logisim project 2024-1_guia17.circ as structural Verilog: 1 circuit, main circuit main
module main (
  input  in_1,
  input  in_2,
  input  in_3,
  input  in_4,
  input  in_5
);

  wire and_1_out, and_2_out, and_3_out, and_4_out, and_5_out, and_6_out, and_7_out, and_8_out, clock_1_out,
       clock_2_out, not_1_out, not_2_out, not_3_out, t_ff_1_q, t_ff_1_qn, t_ff_2_qn, t_ff_3_q, t_ff_4_qn;

  not not_1 (not_1_out, in_2);
  not not_2 (not_2_out, in_1);
  not not_3 (not_3_out, in_3);
  and and_1 (and_1_out, in_2, not_3_out);
  and and_2 (and_2_out, in_1, in_2);
  and and_3 (and_3_out, in_1, in_2, in_3);
  and and_4 (and_4_out, not_2_out, not_1_out, in_3);
  and and_5 (and_5_out, in_1, in_2, in_3);
  and and_6 (and_6_out, not_2_out, not_1_out, in_3);
  and and_7 (and_7_out, in_1, in_2);
  and and_8 (and_8_out, in_1, in_2, in_3);
  // OR_Gate or_1 has open pins: in1=and_3_out, in3=and_4_out, out=open
  // OR_Gate or_2 has open pins: in1=and_5_out, in3=and_6_out, out=open
  Clock clock_1 (.out(clock_1_out));
  Clock clock_2 (.out(clock_2_out));
  T_Flip_Flop t_ff_1 (.clk(clock_1_out), .T(in_4), .Q(t_ff_1_q), .Qn(t_ff_1_qn));  // open: preset, reset, en
  T_Flip_Flop t_ff_2 (.clk(clock_2_out), .T(in_5), .Qn(t_ff_2_qn));  // open: Q, preset, reset, en
  T_Flip_Flop t_ff_3 (.clk(t_ff_1_q), .T(in_4), .Q(t_ff_3_q));  // open: Qn, preset, reset, en
  T_Flip_Flop t_ff_4 (.clk(t_ff_2_qn), .T(in_5), .Qn(t_ff_4_qn));  // open: Q, preset, reset, en
  T_Flip_Flop t_ff_5 (.clk(t_ff_3_q), .T(in_4));  // open: Q, Qn, preset, reset, en
  T_Flip_Flop t_ff_6 (.clk(t_ff_4_qn), .T(in_5));  // open: Q, Qn, preset, reset, en

  // Notes on the sheet:
  //   Questões 1 a 5
  //   1
  //   Db
  //   Da
  //   2
  //   3
  //   SaRa
  //   SbRb
  //   JaKa
  //   JbKb
  //   4
  //   5
endmodule
