// Logisim project Ex01.circ as structural Verilog: 5 circuits, main circuit main
module main (
  input  Ci,
  input  A0,
  input  A1,
  input  A2,
  input  A3,
  input  B0,
  input  B1,
  input  B2,
  input  B3,
  output S0,
  output S1,
  output S2,
  output S3,
  output Co
);

  wire decodificado_1_s, decodificado_1_t, decodificado_1_u, decodificado_1_v, decodificado_1_w,
       decodificado_1_x, decodificado_1_y, decodificado_1_z, decodificado_2_s, decodificado_2_t,
       decodificado_2_u, decodificado_2_v, decodificado_2_w, decodificado_2_x, decodificado_2_y,
       decodificado_2_z, decodificado_3_s, decodificado_3_t, decodificado_3_u, decodificado_3_v,
       decodificado_3_w, decodificado_3_x, decodificado_3_y, decodificado_3_z;

  decodificado decodificado_1 (
    .a(A0), .b(A1), .c(A2), .d(A3), .x(decodificado_1_x), .y(decodificado_1_y), .z(decodificado_1_z),
    .u(decodificado_1_u), .v(decodificado_1_v), .w(decodificado_1_w), .s(decodificado_1_s),
    .t(decodificado_1_t));
  decodificado decodificado_2 (
    .a(B3), .b(B2), .c(B1), .d(B0), .x(decodificado_2_x), .y(decodificado_2_y), .z(decodificado_2_z),
    .u(decodificado_2_u), .v(decodificado_2_v), .w(decodificado_2_w), .s(decodificado_2_s),
    .t(decodificado_2_t));
  _7_Segment_Display u_7_segment_display_1 (
    .g(decodificado_1_u), .f(decodificado_1_z), .a(decodificado_1_y), .b(decodificado_1_x),
    .e(decodificado_1_v), .d(decodificado_1_w), .c(decodificado_1_s), .dp(decodificado_1_t));
  somador_4bits somador_4bits_1 (
    .Ci(Ci), .A0(A0), .A1(A1), .A2(A2), .A3(A3), .B0(B0), .B1(B1), .B2(B2), .B3(B3), .S0(S0), .S1(S1),
    .S2(S2), .S3(S3), .Co(Co));
  _7_Segment_Display u_7_segment_display_2 (
    .g(decodificado_2_u), .f(decodificado_2_z), .a(decodificado_2_y), .b(decodificado_2_x),
    .e(decodificado_2_v), .d(decodificado_2_w), .c(decodificado_2_s), .dp(decodificado_2_t));
  decodificado decodificado_3 (
    .a(S0), .b(S1), .c(S2), .d(S3), .x(decodificado_3_x), .y(decodificado_3_y), .z(decodificado_3_z),
    .u(decodificado_3_u), .v(decodificado_3_v), .w(decodificado_3_w), .s(decodificado_3_s),
    .t(decodificado_3_t));
  _7_Segment_Display u_7_segment_display_3 (
    .g(decodificado_3_u), .f(decodificado_3_z), .a(decodificado_3_y), .b(decodificado_3_x),
    .e(decodificado_3_v), .d(decodificado_3_w), .c(decodificado_3_s), .dp(decodificado_3_t));
endmodule

module meio_somador (
  input  A0,
  input  B0,
  output S,
  output cOut
);

  xor xor_1 (S, A0, B0);
  and and_1 (cOut, A0, B0);
endmodule

module somador_completo (
  input  A0,
  input  B0,
  input  Ci_0,
  output S0,
  output Co_0
);

  wire meio_somador_1_cout, meio_somador_1_s, meio_somador_2_cout;

  meio_somador meio_somador_1 (.A0(A0), .B0(B0), .S(meio_somador_1_s), .cOut(meio_somador_1_cout));
  meio_somador meio_somador_2 (.A0(meio_somador_1_s), .B0(Ci_0), .S(S0), .cOut(meio_somador_2_cout));
  or or_1 (Co_0, meio_somador_2_cout, meio_somador_1_cout);
endmodule

module somador_4bits (
  input  Ci,
  input  A0,
  input  A1,
  input  A2,
  input  A3,
  input  B0,
  input  B1,
  input  B2,
  input  B3,
  output S0,
  output S1,
  output S2,
  output S3,
  output Co
);

  wire somador_completo_1_co_0, somador_completo_2_co_0, somador_completo_3_co_0, xor_1_out;

  xor xor_1 (xor_1_out, somador_completo_2_co_0, somador_completo_3_co_0);
  LED Overflow (.in(xor_1_out));
  somador_completo somador_completo_1 (.A0(A0), .B0(B0), .Ci_0(Ci), .S0(S0), .Co_0(somador_completo_1_co_0));
  somador_completo somador_completo_2 (
    .A0(A1), .B0(B1), .Ci_0(somador_completo_1_co_0), .S0(S1), .Co_0(somador_completo_2_co_0));
  somador_completo somador_completo_3 (
    .A0(A2), .B0(B2), .Ci_0(somador_completo_2_co_0), .S0(S2), .Co_0(somador_completo_3_co_0));
  somador_completo somador_completo_4 (.A0(A3), .B0(B3), .Ci_0(somador_completo_3_co_0), .S0(S3), .Co_0(Co));
endmodule

module decodificado (
  input  a,
  input  b,
  input  c,
  input  d,
  output x,
  output y,
  output z,
  output u,
  output v,
  output w,
  output s,
  output t
);

  wire and_1_out, and_2_out, and_3_out, and_4_out, and_5_out, and_6_out, and_7_out, and_8_out, and_9_out,
       and_10_out, and_11_out, and_12_out, and_13_out, and_14_out, and_15_out, and_16_out, and_17_out,
       and_18_out, and_19_out, and_20_out, and_21_out, and_22_out, not_1_out, not_2_out, not_3_out, not_4_out;

  not not_1 (not_1_out, a);
  not not_2 (not_2_out, b);
  not not_3 (not_3_out, c);
  not not_4 (not_4_out, d);
  and and_1 (and_1_out, c, not_4_out);
  and and_2 (and_2_out, a, not_2_out);
  and and_3 (and_3_out, not_1_out, b);
  and and_4 (and_4_out, a, not_2_out);
  and and_5 (and_5_out, not_1_out, not_3_out, not_4_out);
  and and_6 (and_6_out, a, c, not_4_out);
  and and_7 (and_7_out, not_2_out, not_4_out);
  and and_8 (and_8_out, not_1_out, c);
  and and_9 (and_9_out, not_1_out, b, d);
  and and_10 (and_10_out, a, not_2_out, not_3_out);
  and and_11 (and_11_out, a, not_4_out);
  and and_12 (and_12_out, b, c);
  and and_13 (and_13_out, not_2_out, not_4_out);
  and and_14 (and_14_out, b, c, d);
  and and_15 (and_15_out, not_2_out, not_4_out);
  and and_16 (and_16_out, c, not_4_out);
  and and_17 (and_17_out, a, not_2_out, c);
  and and_18 (and_18_out, a, b, not_3_out, d);
  and and_19 (and_19_out, not_2_out, c, d);
  and and_20 (and_20_out, b, c, not_4_out);
  and and_21 (and_21_out, not_1_out, b);
  and and_22 (and_22_out, a, not_2_out);
  or or_1 (x, and_1_out, and_2_out);
  or or_2 (y, and_3_out, and_4_out, and_5_out, and_6_out);
  or or_3 (z, and_7_out, and_8_out, and_9_out, and_10_out, and_11_out, and_12_out);
  or or_4 (u, and_13_out, and_14_out);
  or or_5 (v, and_15_out, and_16_out, and_17_out, and_18_out);
  or or_6 (w, and_19_out, and_20_out);
  or or_7 (s, not_3_out, d, and_21_out, and_22_out);

  assign t = 1'b0;
endmodule
