// Logisim project Ex02.circ as structural Verilog
module ULA_1bit (
  input  Cin,
  input  Binvert,
  input  [1:0] Operation,
  input  a,
  input  b,
  output Result,
  output Cout
);

  wire adder_1_out, and_1_out, multiplexer_1_out, not_1_out, not_2_out, or_1_out;

  not not_1 (not_1_out, b);
  Multiplexer multiplexer_1 (.in0(b), .in1(not_1_out), .out(multiplexer_1_out), .sel(Binvert));
  and and_1 (and_1_out, a, multiplexer_1_out);
  or or_1 (or_1_out, a, multiplexer_1_out);
  not not_2 (not_2_out, a);
  Adder #(.width(1)) adder_1 (.a(a), .b(multiplexer_1_out), .out(adder_1_out), .cin(Cin), .cout(Cout));
  Multiplexer #(.select(2)) multiplexer_2 (
    .in0(and_1_out), .in1(or_1_out), .in2(not_2_out), .in3(adder_1_out), .out(Result), .sel(Operation));
endmodule

module ULA_4bit (
  input  Binvert,
  input  [1:0] Operation,
  input  B3,
  input  B2,
  input  B1,
  input  B0,
  input  A3,
  input  A2,
  input  A1,
  input  A0,
  output S0,
  output S1,
  output S2,
  output S3,
  output Cout
);

  wire ULA0_cout, ULA1_cout, ULA2_cout;

  ULA_1bit ULA0 (
    .a(A0), .b(B0), .Binvert(Binvert), .Cin(Binvert), .Operation(Operation), .Cout(ULA0_cout), .Result(S0));
  ULA_1bit ULA1 (
    .a(A1), .b(B1), .Binvert(Binvert), .Cin(ULA0_cout), .Operation(Operation), .Cout(ULA1_cout), .Result(S1));
  ULA_1bit ULA2 (
    .a(A2), .b(B2), .Binvert(Binvert), .Cin(ULA1_cout), .Operation(Operation), .Cout(ULA2_cout), .Result(S2));
  ULA_1bit ULA3 (.a(A3), .b(B3), .Binvert(Binvert), .Cin(ULA2_cout), .Operation(Operation), .Cout(Cout), .Result(S3));
endmodule
